// Logisim project LC-3.circ as structural Verilog: 18 circuits, main circuit main
module main (
  input  Reset,
  output out_2,
  output out_3,
  output out_4,
  output out_5,
  output out_6,
  output out_7,
  output out_8,
  output [15:0] out_9,
  output [15:0] out_10,
  output [15:0] out_11,
  output [15:0] out_12,
  output [15:0] out_13,
  output [15:0] out_14,
  output [15:0] out_15,
  output [15:0] out_16,
  output [15:0] out_17,
  output halt,
  output [15:0] out_19,
  output [15:0] out_20,
  output [15:0] out_21,
  output [15:0] out_22
);

  wire decodeir_1_sti___ldi, decodeir_1_writer7, decodeir_1_writereg, getcst_1_usecst, or16_1_out_2,
       or16_2_out_2, PostExec, PostFetch, ramctrl_1_memload, ramctrl_1_memstore, WriteR7;
  wire [2:0] nzp_1_nzp;
  wire [15:0] getcst_1_cst, RegIN, registres_1_out_sr1, registres_1_out_sr2, RES;

  RegPC regpc_1 (
    .PC(out_9), .IR(out_10), .R(registres_1_out_sr1), .TestNZP(out_5), .Jump(out_4), .H(out_3), .Reset(Reset));
  BiClock biclock_1 (.reset(Reset), .Fetch(out_2), .Exec(out_3), .PostFetch(PostFetch), .PostExec(PostExec));
  // Probe on out_9
  GetAddr getaddr_1 (
    .PC(out_9), .R(registres_1_out_sr1), .IR(out_10), .Addr(out_11), .Fetch(out_2), .MemOUT(out_13),
    .PostFetch(PostFetch));
  // Probe on out_11
  // Probe on out_12
  // Probe on out_13
  RAM #(.addrWidth(16), .dataWidth(16), .bus("separate")) ram_1 (
    .addr(out_11), .din(out_12), .data(out_13), .str(ramctrl_1_memstore), .clk(ramctrl_1_memstore),
    .ld(ramctrl_1_memload));  // open: sel, clr
  LED led_1 (.in(out_6));
  RamCtrl ramctrl_1 (
    .Store(out_7), .Fetch(out_2), .Exec(out_3), .Load(out_6), .MemStore(ramctrl_1_memstore),
    .MemLoad(ramctrl_1_memload), .LDI_nSTI(decodeir_1_sti___ldi), .PostFetch(PostFetch), .PostExec(PostExec));
  LED led_2 (.in(out_7));
  Register #(.width(16), .trigger("falling")) RegIR (.D(out_13), .Q(out_10), .clk(out_2));  // open: en, clr
  DecodeIR decodeir_1 (
    .IR(out_10), .Load(out_6), .Store(out_7), .WriteReg(decodeir_1_writereg), .Jump(out_4),
    .STI___LDI(decodeir_1_sti___ldi), .WriteR7(decodeir_1_writer7));
  and and_1 (WriteR7, decodeir_1_writer7, out_3);
  // Probe on out_10[11:9]
  // Probe on out_10[8:6]
  Registres registres_1 (
    .SR1(out_10[8:6]), .IN(RegIN), .SR2(out_10[2:0]), .WriteReg(out_8), .DR_SR(out_10[11:9]),
    .OUT_SR1(registres_1_out_sr1), .OUT_SR2(registres_1_out_sr2), .OUT_SR(out_12), .R0(out_14), .R1(out_15),
    .R2(out_16), .R3(out_17), .R4(out_19), .R5(out_20), .R6(out_21), .R7(out_22), .WriteR7(WriteR7));
  // Probe on out_10[2:0]
  // Probe on registres_1_out_sr1
  ALU alu_1 (
    .UseCst(getcst_1_usecst), .e2(out_10[15:14]), .Input1(registres_1_out_sr1), .Input2(registres_1_out_sr2),
    .Cst(getcst_1_cst), .Output(RES));
  // Probe on getcst_1_cst
  GetCst getcst_1 (.IR(out_10), .Cst(getcst_1_cst), .UseCst(getcst_1_usecst));
  // Probe on out_10[15:14]
  and and_2 (out_8, decodeir_1_writereg, out_3);
  // Probe on registres_1_out_sr2
  Or16 or16_1 (.in_1(out_10), .out_2(or16_1_out_2));
  Or16 or16_2 (.in_1(out_9), .out_2(or16_2_out_2));
  // Probe on out_14
  // Probe on out_15
  // Probe on out_16
  // Probe on out_17
  // Probe on out_19
  // Probe on out_20
  // Probe on out_21
  // Probe on out_22
  // Probe on RES
  NZP nzp_1 (.RES(RegIN), .NZP(nzp_1_nzp), .IR(out_10), .TestNZP(out_5), .WriteReg(out_8));
  // Probe on nzp_1_nzp
  and and_3 (halt, ~or16_1_out_2, or16_2_out_2);  // AND_Gate
  EntryReg entryreg_1 (.RES(RES), .MemOUT(out_13), .RegIN(RegIN), .PC(out_9), .IR(out_10));
  // Probe on RegIN
  LED led_3 (.in(PostExec));
  LED led_4 (.in(out_2));
  LED led_5 (.in(PostFetch));
  LED led_6 (.in(out_3));

  // Other names for the same wires on the sheet: Addr[15:0] = out_11; Condition = out_5; Exec = out_3; Fetch = out_2;
  //   IR[15:0] = out_10; JumpInstr = out_4; Load = out_6; MemIN[15:0] = out_12; MemOUT[15:0] = out_13;
  //   PC[15:0] = out_9; R0[15:0] = out_14; R1[15:0] = out_15; R2[15:0] = out_16; R3[15:0] = out_17; R4[15:0] = out_19;
  //   R5[15:0] = out_20; R6[15:0] = out_21; R7[15:0] = out_22; Store = out_7; WriteReg = out_8

  // Notes on the sheet:
  //   R
  //   IR
  //   R
  //   IR
  //   RAM
  //   LDI / STI
  //   Traces (NE PAS MODIFIER)______________________________________________________________________________________________________
  //   GetOp
  //   GetRegs
  //   Arret des traces au 1er NOP
endmodule

module ALU (
  input  [15:0] Input1,
  input  [15:0] Input2,
  input  [15:0] Cst,
  input  UseCst,
  input  [1:0] e2,
  output [15:0] Output
);

  wire [15:0] adder_1_out, AND_out, multiplexer_1_out, NOT___XOR_out;

  Multiplexer #(.width(16), .enable("false")) multiplexer_1 (
    .in0(Input2), .in1(Cst), .out(multiplexer_1_out), .sel(UseCst));
  Adder #(.width(16)) adder_1 (.a(multiplexer_1_out), .b(Input1), .out(adder_1_out));  // open: cin, cout
  assign AND_out = Input1 & multiplexer_1_out;  // AND_Gate AND, 16 bits wide
  Multiplexer #(.select(2), .width(16), .enable("false")) multiplexer_2 (
    .in0(adder_1_out), .in1(AND_out), .in2(NOT___XOR_out), .out(Output), .sel(e2));  // open: in3
  assign NOT___XOR_out = Input1 ^ multiplexer_1_out;  // XOR_Gate NOT___XOR, 16 bits wide

  // Notes on the sheet:
  //   ADD
  //   0 => Input2
  //   1 => Cst
  //   0 => ADD
  //   1 => AND
  //   2 => NOT / XOR
endmodule

module BiClock (
  input  reset,
  output Fetch,
  output PostFetch,
  output Exec,
  output PostExec
);

  wire and_1_out, horloge_out, not_1_out, register_1_q;

  not not_1 (not_1_out, register_1_q);
  Clock horloge (.out(horloge_out));
  Register #(.width(1), .trigger("falling")) register_1 (
    .D(not_1_out), .Q(register_1_q), .clk(horloge_out), .clr(reset));  // open: en
  and and_1 (and_1_out, horloge_out, ~reset);  // AND_Gate
  and and_2 (Fetch, ~register_1_q, and_1_out);  // AND_Gate
  and and_3 (PostFetch, register_1_q, ~and_1_out);  // AND_Gate
  and and_4 (Exec, register_1_q, and_1_out);
  and and_5 (PostExec, ~register_1_q, ~and_1_out);  // AND_Gate

  // Notes on the sheet:
  //   Ce module divise une horloge en deux sous-horloges alternées
  //   registre 1-bit
  //   Enable
  //   select : 0 / 1
  //   Chronogrammes :
  //   Horloge:     0101 0101
  //   0100 0100
  //   0010 0010
  //   0001 0001
  //   1000 1000
endmodule

module GetAddr (
  input  [15:0] PC,
  input  [15:0] R,
  input  [15:0] MemOUT,
  input  PostFetch,
  input  [15:0] IR,
  input  Fetch,
  output [15:0] Addr
);

  wire and_1_out, LD_ST_out, LDI_STI_out, LDR_STR_out;
  wire [1:0] or_1_out;
  wire [15:0] adder_2_out, multiplexer_1_out, Off6, Off9, PC_Off9, register_1_q;

  Register #(.width(16), .trigger("falling")) register_1 (
    .D(MemOUT), .Q(register_1_q), .clk(PostFetch));  // open: en, clr
  // Probe on Off6
  Offset6 offset6_1 (.IR(IR), .Off6(Off6));
  // Probe on Off9
  Offset9 offset9_1 (.IR(IR), .Off9(Off9));
  Adder #(.width(16)) adder_1 (.a(PC), .b(Off9), .out(PC_Off9), .cin(1'b1));  // open: cout
  Adder #(.width(16)) adder_2 (.a(Off6), .b(R), .out(adder_2_out));  // open: cin, cout
  and and_1 (and_1_out, IR[13], ~Fetch);  // AND_Gate
  Multiplexer #(.width(16), .enable("false")) multiplexer_1 (
    .in0(register_1_q), .in1(PC_Off9), .out(multiplexer_1_out), .sel(PostFetch));
  // Probe on PC
  // Probe on PC_Off9
  // Probe on adder_2_out
  // Probe on multiplexer_1_out
  and LD_ST (LD_ST_out, ~IR[15], ~IR[14], and_1_out);  // AND_Gate
  Multiplexer #(.select(2), .width(16), .enable("false")) multiplexer_2 (
    .in0(PC), .in1(PC_Off9), .in2(adder_2_out), .in3(multiplexer_1_out), .out(Addr), .sel(or_1_out));
  // Probe on or_1_out
  or or_1 (or_1_out[0], LD_ST_out, LDI_STI_out);
  or or_2 (or_1_out[1], LDR_STR_out, LDI_STI_out);
  and LDR_STR (LDR_STR_out, ~IR[15], IR[14], and_1_out);  // AND_Gate
  and LDI_STI (LDI_STI_out, IR[15], ~IR[14], and_1_out);  // AND_Gate

  // Notes on the sheet:
  //   PC + off9
  //   R + off6
  //   non fetch et (Load ou Store)
  //   0 => PC
  //   1 => LD/ST (PC + off9)
  //   2 => LDR/STR (R + off6)
  //   3 => LDI/STI
  //   Adresse Memoire
endmodule

module DecodeIR (
  input  [15:0] IR,
  output Jump,
  output WriteR7,
  output Load,
  output Store,
  output STI___LDI,
  output WriteReg
);

  wire Arithm_out, LDI_STI_out, or_2_out;

  and u_Jump (Jump, ~IR[13], ~IR[12]);  // AND_Gate
  and Arithm (Arithm_out, ~IR[13], IR[12]);  // AND_Gate
  and u_Load (Load, IR[13], ~IR[12]);  // AND_Gate
  and u_Store (Store, IR[13], IR[12]);
  and LDI_STI (LDI_STI_out, IR[15], ~IR[14]);  // AND_Gate
  or or_1 (WriteReg, Arithm_out, Load);
  and and_1 (WriteR7, Jump, ~IR[15], IR[14]);  // AND_Gate
  or or_2 (or_2_out, Store, Load);
  // Probe on Arithm_out
  and and_2 (STI___LDI, or_2_out, LDI_STI_out);
endmodule

module GetCst (
  input  [15:0] IR,
  output [15:0] Cst,
  output UseCst
);

  assign Cst = {{11{IR[4]}}, IR[4:0]};  // Bit_Extender bit_extender_1

  assign UseCst = IR[5];
endmodule

module NZP (
  input  WriteReg,
  input  [15:0] RES,
  input  [15:0] IR,
  output [2:0] NZP,
  output TestNZP
);

  wire and_2_out, and_3_out, and_4_out, not_1_out, or16_1_out_2;
  wire [1:0] and_1_out;

  Or16 or16_1 (.in_1(RES), .out_2(or16_1_out_2));
  not not_1 (not_1_out, RES[15]);
  not not_2 (and_1_out[1], or16_1_out_2);
  and and_1 (and_1_out[0], not_1_out, ~and_1_out[1]);  // AND_Gate
  // Probe on {RES[15], and_1_out}
  Verrou3bits verrou3bits_1 (.write(WriteReg), .Input({RES[15], and_1_out}), .Output(NZP));
  and and_2 (and_2_out, NZP[0], IR[9]);
  and and_3 (and_3_out, NZP[1], IR[10]);
  and and_4 (and_4_out, NZP[2], IR[11]);
  or or_1 (TestNZP, and_2_out, and_3_out, and_4_out);

  // Notes on the sheet:
  //   (Instruction mettant à jour NZP)
  //   (Resultat du calcul courant)
  //   (Instruction courante)
  //   Test s'il y a au moins un bit à 1
  //   Test si positif
  //   Valeur actuel du registre d'état NZP
  //   1 = z
  //   0 = p
  //   2 = n
  //   Test du NZP
  //   11 = n
  //   10 = z
  //   9 = p
  //   Test de saut
endmodule

// Off6
module Offset6 (
  input  [15:0] IR,
  output [15:0] Off6
);

  assign Off6 = {{10{IR[5]}}, IR[5:0]};  // Bit_Extender bit_extender_1
endmodule

// Off9
module Offset9 (
  input  [15:0] IR,
  output [15:0] Off9
);

  assign Off9 = {{7{IR[8]}}, IR[8:0]};  // Bit_Extender bit_extender_1
endmodule

// Off11
module Offset11 (
  input  [15:0] IR,
  output [15:0] Off11
);

  assign Off11 = {{5{IR[10]}}, IR[10:0]};  // Bit_Extender bit_extender_1
endmodule

module Or16 (
  input  [15:0] in_1,
  output out_2
);

  wire [3:0] or_1_out;

  assign or_1_out = in_1[3:0] | in_1[7:4] | in_1[11:8] | in_1[15:12];  // OR_Gate or_1, 4 bits wide
  or or_2 (out_2, or_1_out[0], or_1_out[1], or_1_out[2], or_1_out[3]);
endmodule

module RamCtrl (
  input  PostExec,
  input  Fetch,
  input  PostFetch,
  input  Exec,
  input  Load,
  input  LDI_nSTI,
  input  Store,
  output MemLoad,
  output MemStore
);

  wire and_1_out, and_2_out, and_3_out, and_4_out;

  and and_1 (and_1_out, PostExec, LDI_nSTI, Store);
  and and_2 (and_2_out, PostFetch, LDI_nSTI);
  and and_3 (and_3_out, Exec, Load);
  and and_4 (and_4_out, Exec, ~LDI_nSTI, Store);  // AND_Gate
  or or_1 (MemLoad, Fetch, and_3_out, and_2_out);
  or or_2 (MemStore, and_4_out, and_1_out);

  // Notes on the sheet:
  //   PostFetch & LDI/STI
  //   PostExec & LDI/STI & Store
  //   Exec & Load
  //   Exec & non LDI/STI & Store
endmodule

module Registres (
  input  [2:0] SR1,
  input  [15:0] IN,
  input  [2:0] SR2,
  input  WriteReg,
  input  [2:0] DR_SR,
  input  WriteR7,
  output [15:0] R0,
  output [15:0] OUT_SR1,
  output [15:0] R1,
  output [15:0] R2,
  output [15:0] R3,
  output [15:0] OUT_SR2,
  output [15:0] R4,
  output [15:0] R5,
  output [15:0] OUT_SR,
  output [15:0] R6,
  output [15:0] R7
);

  wire decoder_1_out0, decoder_1_out1, decoder_1_out2, decoder_1_out3, decoder_1_out4, decoder_1_out5,
       decoder_1_out6, decoder_1_out7, or_1_out;

  Decoder #(.select(3), .disabled(0)) decoder_1 (
    .out0(decoder_1_out0), .out1(decoder_1_out1), .out2(decoder_1_out2), .out3(decoder_1_out3),
    .out4(decoder_1_out4), .out5(decoder_1_out5), .out6(decoder_1_out6), .out7(decoder_1_out7), .sel(DR_SR),
    .en(WriteReg));
  Register #(.width(16), .trigger("falling")) u_R0 (.D(IN), .Q(R0), .clk(decoder_1_out0));  // open: en, clr
  Register #(.width(16), .trigger("falling")) u_R1 (.D(IN), .Q(R1), .clk(decoder_1_out1));  // open: en, clr
  Register #(.width(16), .trigger("falling")) u_R2 (.D(IN), .Q(R2), .clk(decoder_1_out2));  // open: en, clr
  Register #(.width(16), .trigger("falling")) u_R3 (.D(IN), .Q(R3), .clk(decoder_1_out3));  // open: en, clr
  Register #(.width(16), .trigger("falling")) u_R4 (.D(IN), .Q(R4), .clk(decoder_1_out4));  // open: en, clr
  Register #(.width(16), .trigger("falling")) u_R5 (.D(IN), .Q(R5), .clk(decoder_1_out5));  // open: en, clr
  Register #(.width(16), .trigger("falling")) u_R6 (.D(IN), .Q(R6), .clk(decoder_1_out6));  // open: en, clr
  Register #(.width(16), .trigger("falling")) u_R7 (.D(IN), .Q(R7), .clk(or_1_out));  // open: en, clr
  or or_1 (or_1_out, decoder_1_out7, WriteR7);
  Multiplexer #(.select(3), .width(16), .enable("false")) multiplexer_1 (
    .in0(R0), .in1(R1), .in2(R2), .in3(R3), .in4(R4), .in5(R5), .in6(R6), .in7(R7), .out(OUT_SR1), .sel(SR1));
  Multiplexer #(.select(3), .width(16), .enable("false")) multiplexer_2 (
    .in0(R0), .in1(R1), .in2(R2), .in3(R3), .in4(R4), .in5(R5), .in6(R6), .in7(R7), .out(OUT_SR2), .sel(SR2));
  Multiplexer #(.select(3), .width(16), .enable("false")) multiplexer_3 (
    .in0(R0), .in1(R1), .in2(R2), .in3(R3), .in4(R4), .in5(R5), .in6(R6), .in7(R7), .out(OUT_SR), .sel(DR_SR));
endmodule

module RegPC (
  input  [15:0] IR,
  input  H,
  input  Reset,
  input  [15:0] R,
  input  Jump,
  input  TestNZP,
  output [15:0] PC
);

  wire BR_out, JMP_out, JSR_R_out;
  wire [1:0] or_2_out;
  wire [15:0] adder_1_out, adder_2_out, adder_3_out, multiplexer_1_out, multiplexer_2_out, Off9, Off11;

  Adder #(.width(16)) adder_1 (.a(PC), .b({16{1'b0}}), .out(adder_1_out), .cin(1'b1));  // open: cout
  Offset9 offset9_1 (.IR(IR), .Off9(Off9));
  Offset11 offset11_1 (.IR(IR), .Off11(Off11));
  Adder #(.width(16)) adder_2 (.a(adder_1_out), .b(Off11), .out(adder_2_out));  // open: cin, cout
  Adder #(.width(16)) adder_3 (.a(adder_1_out), .b(Off9), .out(adder_3_out));  // open: cin, cout
  Multiplexer #(.width(16), .enable("false")) multiplexer_1 (
    .in0(R), .in1(adder_2_out), .out(multiplexer_1_out), .sel(IR[11]));
  and JSR_R (JSR_R_out, ~IR[15], IR[14], Jump);  // AND_Gate
  and JMP (JMP_out, IR[15], IR[14], Jump);
  Multiplexer #(.select(2), .width(16), .enable("false")) multiplexer_2 (
    .in0(adder_1_out), .in1(adder_3_out), .in2(R), .in3(multiplexer_1_out), .out(multiplexer_2_out),
    .sel(or_2_out));
  or or_1 (or_2_out[1], JMP_out, JSR_R_out);
  or or_2 (or_2_out[0], JSR_R_out, BR_out);
  and BR (BR_out, ~IR[15], ~IR[14], Jump, TestNZP);  // AND_Gate
  Register #(.width(16), .trigger("falling")) u_PC (.D(multiplexer_2_out), .Q(PC), .clk(H), .clr(Reset));  // open: en
  // Probe on PC

  // Notes on the sheet:
  //   PC <- PC + 1
  //   PC + off11
  //   PC + offset9
  //   0 => JSRR (R)
  //   1 => JSR (PC + off11)
  //   0 => PC
  //   1 => BR
  //   2 => JMP
  //   3 => JSR / JSRR
  //   BR et NZP
endmodule

module EntryReg (
  input  [15:0] RES,
  input  [15:0] MemOUT,
  input  [15:0] PC,
  input  [15:0] IR,
  output [15:0] RegIN
);

  wire JSR_JSRR_out, LEA_out;
  wire [1:0] Load_out;
  wire [15:0] adder_1_out, adder_2_out, offset9_1_off9;

  Offset9 offset9_1 (.IR(IR), .Off9(offset9_1_off9));
  Adder #(.width(16)) adder_1 (.a(PC), .b({16{1'b0}}), .out(adder_1_out), .cin(1'b1));  // open: cout
  Adder #(.width(16)) adder_2 (.a(PC), .b(offset9_1_off9), .out(adder_2_out), .cin(1'b1));  // open: cout
  and Load (Load_out[0], ~IR[12], IR[13]);  // AND_Gate
  Multiplexer #(.select(2), .width(16), .enable("false")) multiplexer_1 (
    .in0(RES), .in1(MemOUT), .in2(adder_1_out), .in3(adder_2_out), .out(RegIN), .sel(Load_out));
  // Probe on Load_out
  or or_1 (Load_out[1], LEA_out, JSR_JSRR_out);
  and LEA (LEA_out, Load_out[0], IR[14], IR[15]);
  and JSR_JSRR (JSR_JSRR_out, ~IR[12], ~IR[13], IR[14], ~IR[15]);  // AND_Gate

  // Notes on the sheet:
  //   PC + off9
  //   PC + 1
  //   0 => RES
  //   1 => MemOUT
  //   2 => PC +1
  //   3 => LEA
endmodule

module Verrou (
  input  h,
  input  e,
  output s
);

  wire and_1_out, and_2_out, not_1_out, not_2_out, not_3_out, or_1_out;

  not not_1 (not_1_out, e);
  and and_1 (and_1_out, h, not_1_out);
  and and_2 (and_2_out, h, e);
  not not_2 (not_2_out, s);
  or or_1 (or_1_out, and_1_out, not_2_out);
  not not_3 (not_3_out, or_1_out);
  or or_2 (s, not_3_out, and_2_out);
endmodule

module Verrou3bits (
  input  write,
  input  [2:0] Input,
  output [2:0] Output
);

  Verrou verrou_1 (.h(write), .e(Input[0]), .s(Output[0]));
  Verrou verrou_2 (.h(write), .e(Input[1]), .s(Output[1]));
  Verrou verrou_3 (.h(write), .e(Input[2]), .s(Output[2]));
endmodule

module Verrou16bits (
  input  write,
  input  [15:0] Input,
  output [15:0] Output
);

  Verrou verrou_1 (.h(write), .e(Input[0]), .s(Output[0]));
  Verrou verrou_2 (.h(write), .e(Input[1]), .s(Output[1]));
  Verrou verrou_3 (.h(write), .e(Input[2]), .s(Output[2]));
  Verrou verrou_4 (.h(write), .e(Input[3]), .s(Output[3]));
  Verrou verrou_5 (.h(write), .e(Input[4]), .s(Output[4]));
  Verrou verrou_6 (.h(write), .e(Input[5]), .s(Output[5]));
  Verrou verrou_7 (.h(write), .e(Input[6]), .s(Output[6]));
  Verrou verrou_8 (.h(write), .e(Input[7]), .s(Output[7]));
  Verrou verrou_9 (.h(write), .e(Input[8]), .s(Output[8]));
  Verrou verrou_10 (.h(write), .e(Input[9]), .s(Output[9]));
  Verrou verrou_11 (.h(write), .e(Input[10]), .s(Output[10]));
  Verrou verrou_12 (.h(write), .e(Input[11]), .s(Output[11]));
  Verrou verrou_13 (.h(write), .e(Input[12]), .s(Output[12]));
  Verrou verrou_14 (.h(write), .e(Input[13]), .s(Output[13]));
  Verrou verrou_15 (.h(write), .e(Input[14]), .s(Output[14]));
  Verrou verrou_16 (.h(write), .e(Input[15]), .s(Output[15]));
endmodule
